# Fritzing sketch HandWashTimer (saved by Fritzing 0.9.0b)

parts:
  パーツ1 = Arduino Uno (Rev3)
  S1 = Pushbutton [package="[THT]"]
  J1 = Piezo Speaker

nets:
  N1: パーツ1.D12/MISO, J1.pin2
  N2: パーツ1.D2, S1.Pin_4
  N3: パーツ1.GND, S1.Pin_2, J1.pin1
