# Fritzing sketch HandWashTimer85 (saved by Fritzing 0.9.0b)
perfboards: 1

parts:
  Piezzo = Piezo Speaker
  ATTiny85 = IC, DIP package, 8 pins [chip_label=ATTiny85]
  VCC1 = Battery
  T1 = Pushbutton [package="[SMD]"]

nets:
  N1: Piezzo.pin1, ATTiny85.pin4, VCC1.-, T1.Pin_1, T1.Pin_2
  N2: Piezzo.pin2, ATTiny85.pin2
  N3: ATTiny85.pin3, T1.Pin_3, T1.Pin_4
  N4: ATTiny85.pin8, VCC1.+
